# Fritzing sketch Platine Hoerbie (saved by Fritzing 0.9.3b)
circuit board: 6cm x 7cm
breadboards: 1

parts:
  IC2_Gyro = InvenSense MPU6050
  IC3_RFID-Reader = IC, SIP package, 8 pins [chip_label="RFID RC522"]
  LED1 = IC, SIP package, 3 pins [chip_label="RFID RC522"]
  IC4_MP3_Player = DFRobot DFPlayer Mini [part_number=DFR0299]
  SP = IC, SIP package, 3 pins [chip_label="RFID RC522"]
  -_+ = IC, SIP package, 2 pins [chip_label="RFID RC522"]
  IC1_ESP32 = ESP32-38PinWide [part_number="ESP32 - 38Pin"]

nets:
  VCC: IC2_Gyro.VCC, IC3_RFID-Reader.pin1, LED1.pin1, IC4_MP3_Player.VCC, IC1_ESP32.3.3
  GND: IC2_Gyro.GND, IC3_RFID-Reader.pin3, LED1.pin2, IC4_MP3_Player.GND-1, IC4_MP3_Player.GND-2, SP.pin2, -_+.pin2, IC1_ESP32.GND
  N1: IC2_Gyro.SCL, IC1_ESP32.GPIO15
  N2: IC2_Gyro.SDA, IC1_ESP32.GPIO0
  N3: IC3_RFID-Reader.pin2, IC1_ESP32.GPIO22
  N4: IC3_RFID-Reader.pin5, IC1_ESP32.GPIO19
  N5: IC3_RFID-Reader.pin6, IC1_ESP32.GPIO23
  N6: IC3_RFID-Reader.pin7, IC1_ESP32.GPIO18
  N7: IC3_RFID-Reader.pin8, IC1_ESP32.GPIO21
  N8: LED1.pin3, IC1_ESP32.GPIO2
  N9: IC4_MP3_Player.RX, IC1_ESP32.GPIO17
  N10: IC4_MP3_Player.TX, IC1_ESP32.GPIO16
  N11: IC4_MP3_Player.SPK_1, SP.pin1
  N12: IC4_MP3_Player.SPK_2, SP.pin3
  N13: IC4_MP3_Player.BUSY, IC1_ESP32.GPIO4
  N14: -_+.pin1, IC1_ESP32.VIN

notes:
  hoerbert 1.0
  Marko Langer 2020
  s  -  +

custom parts:
  ESP32-38PinWide: Generic 38-Pin ESP32 with wide format (only access to one side of pins on a breadboard) based on Stephen Lilley's HiLetgo ESP-WROOM-32 ESP32 ESP-32S Development Board.
