# Fritzing sketch hoerbie (saved by Fritzing 0.9.3b)
circuit board: 7.28721cm x 5.90552cm
stripboards: 2

parts:
  J3 = Power Jack [package=power_jack_pth]
  SP1 = SPEAKER [package=pcb_mount_speaker]
  IC2 = InvenSense MPU6050
  IC4 = DFRobot DFPlayer Mini [part_number=DFR0299]
  IC3 = RFID RC522 SIP - 8 pins [chip_label="RFID RC522" package="SIP (Single Inline) [THT]"]
  LED1 = RGB LED PL9823 F5 [part_number="PL9823 F5" package="5 mm [THT]"]
  IC1 = ESP32-38PinWide [part_number="ESP32 - 38Pin"]

nets:
  GND: J3.GND, IC2.GND, IC4.GND-1, IC4.GND-2, IC3.GND, LED1.GND, IC1.GND
  N1: J3.PWR, IC1.VIN
  N2: SP1.+, IC4.SPK_1
  N3: SP1.-, IC4.SPK_2
  VCC: IC2.VCC, IC4.VCC, IC3.VCC, LED1.VDD, IC1.3.3
  N4: IC2.SCL, IC1.GPIO15
  N5: IC2.SDA, IC1.GPIO0
  N6: IC4.RX, IC1.GPIO17
  N7: IC4.TX, IC1.GPIO16
  N8: IC4.BUSY, IC1.GPIO4
  N9: IC3.IRQ, IC1.GPIO21
  N10: IC3.NSS, IC1.GPIO18
  N11: IC3.SCK, IC1.GPIO23
  N12: IC3.MOSI, IC1.GPIO19
  N13: IC3.RST, IC1.GPIO22
  N14: LED1.DIN, IC1.GPIO2

custom parts:
  RFID RC522 SIP - 8 pins: A SIP stand-in part for RFID RC522 . With 8 pins on a 300 mil single inline package (SIP) footprint.
  RGB LED PL9823 F5: A 5mm tri-color LED with red, green and blue inside. this led includes WS2811 controller.
  ESP32-38PinWide: Generic 38-Pin ESP32 with wide format (only access to one side of pins on a breadboard) based on Stephen Lilley's HiLetgo ESP-WROOM-32 ESP32 ESP-32S Development Board.
