# Fritzing sketch hoerbie (saved by Fritzing 0.9.3b)
circuit board: 7.28721cm x 5.90552cm
stripboards: 1

parts:
  IC1 = ESP32-38PinWide [part_number=ESP32-38PinWide]
  J3 = Power Jack [package=power_jack_pth]
  SP1 = SPEAKER [package=pcb_mount_speaker]
  IC2 = InvenSense MPU6050
  IC4 = DFRobot DFPlayer Mini [part_number=DFR0299]
  IC3 = RFID RC522 SIP - 8 pins [chip_label="RFID RC522" package="SIP (Single Inline) [THT]"]
  IC5 = ws2812b [package="smd 2812b"]

nets:
  VCC: IC1.3.3, IC2.VCC, IC4.VCC, IC5.VDD
  GND: IC1.GND, J3.GND, IC2.GND, IC4.GND-1, IC4.GND-2, IC3.GND, IC5.VSS
  N1: IC1.VIN, J3.PWR
  N2: IC1.GPIO15, IC2.SCL
  N3: IC1.GPIO2, IC5.DIN
  N4: IC1.GPIO0, IC2.SDA
  N5: IC1.GPIO4, IC4.BUSY
  N6: IC1.GPIO16, IC4.TX
  N7: IC1.GPIO17, IC4.RX
  N8: IC1.GPIO18, IC3.NSS
  N9: IC1.GPIO19, IC3.MOSI
  N10: IC1.GPIO21, IC3.IRQ
  N11: IC1.GPIO22, IC3.RST
  N12: IC1.GPIO23, IC3.SCK
  N13: SP1.+, IC4.SPK_1
  N14: SP1.-, IC4.SPK_2

custom parts:
  ESP32-38PinWide: Generic 38-Pin ESP32 with wide format (only access to one side of pins on a breadboard) based on Stephen Lilley's HiLetgo ESP-WROOM-32 ESP32 ESP-32S Development Board.
  RFID RC522 SIP - 8 pins: A SIP stand-in part for RFID RC522 . With 8 pins on a 300 mil single inline package (SIP) footprint.
